# Fritzing sketch Circuito (saved by Fritzing 0.9.3b)
circuit board: 8.46667cm x 5.64444cm
breadboards: 1

parts:
  Componente1 = Arduino Uno (Rev3) - ICSP
  U1 = ESP8266 NodeMCU LoLin module
  S1 = Pushbutton [package=THT]
  R1 = Resistor [tolerance=±5% resistance=10k package=THT]
  R2 = Resistor [tolerance=±5% resistance=10k package=THT]
  R3 = Resistor [tolerance=±5% resistance=10k package=THT]
  R4 = Resistor [tolerance=±5% resistance=10k package=THT]
  S3 = Pushbutton [package=THT]
  S4 = Pushbutton [package=THT]
  S5 = Pushbutton [package=THT]
  R5 = Resistor [tolerance=±5% resistance=220 package="1206 [SMD]"]
  R6 = Resistor [tolerance=±5% resistance=220 package="1206 [SMD]"]
  DI1 = 7-Segment LED Display [package=THT]
  LED1 = LED - 3mm [color="Red (633nm)" package="3 mm [THT]"]
  LED2 = LED - 3mm [color="Yellow (585nm)" package="3 mm [THT]"]
  LED3 = LED - 3mm [color="Blue (430nm)" package="3 mm [THT]"]
  LED4 = LED - 3mm [color="Green (555nm)" package="3 mm [THT]"]
  R7 = Resistor [tolerance=±5% resistance=220 package=THT]
  R8 = Resistor [tolerance=±5% resistance=220 package=THT]
  R9 = Resistor [tolerance=±5% resistance=220 package=THT]
  R10 = Resistor [tolerance=±5% resistance=220 package=THT]

nets:
  N1: Componente1.A0, DI1.cathodeA
  N2: Componente1.A1, DI1.cathodeF
  N3: Componente1.A2, DI1.cathodeG
  N4: Componente1.A3, DI1.cathodeC
  N5: Componente1.A4/SDA, DI1.cathodeD
  N6: Componente1.A5/SCL, DI1.cathodeE
  N7: Componente1.5V, S1.leg0, S3.leg0, S4.leg0, S5.leg0
  N8: Componente1.D8, U1.D2, LED3.anode
  N9: Componente1.D9_PWM, U1.D3, LED2.anode
  N10: Componente1.D11_PWM/MOSI, DI1.cathodeB
  GND: Componente1.GND, U1.GND, R1.Pin_0, R3.Pin_0, R4.Pin_0, R5.Pin_0, R7.Pin_0, R8.Pin_0, R9.Pin_0, R10.Pin_0
  N11: Componente1.D2, S1.leg1, R1.Pin_1
  N12: Componente1.D3_PWM, R2.Pin_1, S5.leg1
  N13: Componente1.D4, R3.Pin_1, S4.leg1
  N14: Componente1.D5_PWM, R4.Pin_1, S3.leg1
  N15: Componente1.D6_PWM, U1.D0, LED1.anode
  N16: Componente1.D7, U1.D1, LED4.anode
  N17: R5.Pin_1, DI1.commAnode#7
  N18: R6.Pin_0, DI1.commAnode#2
  N19: LED1.cathode, R7.Pin_1
  N20: LED2.cathode, R9.Pin_1
  N21: LED3.cathode, R10.Pin_1
  N22: LED4.cathode, R8.Pin_1

custom parts:
  ESP8266 NodeMCU LoLin module: ESP8266 based NodeMCU
